// Logisim project Computador simulador.circ as structural Verilog
module main (
  input  CLEAR
);

  wire ADD, CLK, clock_1_out, EQ, GEQ, GT, HLT, JMP, LEQ, LT, MovRxRA, MovRxRy, MUL, not_1_out, RDM, STR, SUB;
  wire [1:0] Rx, Ry;
  wire [3:0] OPERACAO;
  wire [4:0] CONTADOR;
  wire [7:0] Acumulador, ConteudoRX, ConteudoRY, controlled_buffer_2_out, Input_RAM, RA, RAM, Saida_ROM;

  PC pc_1 (.CONTADOR(CONTADOR), .CLK(CLK), .reset(CLEAR));
  assign CLK = not_1_out ? clock_1_out : 1'bz;  // Controlled_Buffer controlled_buffer_1
  Clock clock_1 (.out(clock_1_out));
  not not_1 (not_1_out, HLT);
  \Decode_instruções  \decode_instruções_1  (
    .Operacao(OPERACAO), .EQ(EQ), .LT(LT), .GT(GT), .LEQ(LEQ), .GEQ(GEQ), .JMP(JMP), .MUL(MUL), .ADD(ADD),
    .SUB(SUB), .MovRxRy(MovRxRy), .MovRxRA(MovRxRA), .RDM(RDM), .STR(STR), .HLT(HLT));
  \Registrador_de_instrução  \registrador_de_instrução_1  (
    .Instrucao_ROM(Saida_ROM), .Ry(Ry), .Rx(Rx), .\Instrução_decodificador (OPERACAO), .CLK(CLK),
    .clear(CLEAR));
  assign controlled_buffer_2_out = MovRxRA ? RA : 8'bz;  // Controlled_Buffer controlled_buffer_2
  assign controlled_buffer_2_out = RDM ? RAM : 8'bz;  // Controlled_Buffer controlled_buffer_3
  assign controlled_buffer_2_out = MovRxRy ? ConteudoRY : 8'bz;  // Controlled_Buffer controlled_buffer_4
  Register u_RA (.D(Acumulador), .Q(RA), .clk(CLK));  // open: en, clr
  ROM #(.addrWidth(5)) rom_1 (.addr(CONTADOR), .data(Saida_ROM));  // open: sel
  RAM #(.addrWidth(2), .bus("separate")) ram_1 (
    .addr(Ry), .din(Input_RAM), .data(RAM), .str(STR), .clk(CLK), .ld(RDM));  // open: sel, clr
  Banco_de_registradores banco_de_registradores_1 (
    .RX(Rx), .CLK(CLK), .Conteudo_RX(ConteudoRX), .Conteudo_Ry(ConteudoRY), .Rx_2(Rx), .Ry(Ry),
    .reset(CLEAR), .Input_banco(controlled_buffer_2_out));
  ULA ula_1 (
    .Entrada_Rx(ConteudoRX), .Entrada_Ry(ConteudoRY), .ADD(ADD), .SUB(SUB), .MUL(MUL), .EQ(EQ), .LT(LT),
    .GT(GT), .GEQ(GEQ), .LEQ(LEQ), .ACULUMADOR(Acumulador));

  // Notes on the sheet:
  //   CONTADOR DE PROGRAMA
  //   DECODIFICADOR DE INSTRUÇÕES 
  //   Registrador de Instrução 
  //   END RAM
  //   END REGISTRADOR
  //   RDM Rx , End; [Rx] ← End. mem dados
  //   MOV Rx , RA	;        [Rx] ← [RA]
  //   MOV Rx , Ry	;        [Rx] ← [Ry]
  //   REGISTRADOR ACUMULADOR
  //   BANCO DE REGISTRADORES
  //   Memoria de programa
  //   Memoria Dados
  //   INSTRUÇÃO
  //   ULA
endmodule

module ULA (
  input  EQ,
  input  [7:0] Entrada_Rx,
  input  LT,
  input  [7:0] Entrada_Ry,
  input  GT,
  input  LEQ,
  input  GEQ,
  input  ADD,
  input  SUB,
  input  MUL,
  output [7:0] ACULUMADOR
);

  wire comparator_1_eq, comparator_2_lt, comparator_3_eq, comparator_3_lt, comparator_4_eq, comparator_4_gt,
       comparator_5_gt, controlled_buffer_4_out, or_1_out, or_2_out, or_3_out, or_4_out;
  wire [7:0] adder_1_out, multiplier_1_out, OutCOMP, OutOP, subtractor_1_out;

  Comparator comparator_1 (.a(Entrada_Rx), .b(Entrada_Ry), .eq(comparator_1_eq));  // open: gt, lt
  Comparator comparator_2 (.a(Entrada_Rx), .b(Entrada_Ry), .lt(comparator_2_lt));  // open: gt, eq
  Comparator comparator_3 (.a(Entrada_Rx), .b(Entrada_Ry), .eq(comparator_3_eq), .lt(comparator_3_lt));  // open: gt
  Comparator comparator_4 (.a(Entrada_Rx), .b(Entrada_Ry), .gt(comparator_4_gt), .eq(comparator_4_eq));  // open: lt
  Comparator comparator_5 (.a(Entrada_Rx), .b(Entrada_Ry), .gt(comparator_5_gt));  // open: eq, lt
  or or_1 (or_1_out, comparator_3_eq, comparator_3_lt);
  or or_2 (or_2_out, comparator_4_gt, comparator_4_eq);
  assign OutOP = ADD ? adder_1_out : 8'bz;  // Controlled_Buffer controlled_buffer_1
  Adder adder_1 (.a(Entrada_Rx), .b(Entrada_Ry), .out(adder_1_out));  // open: cin, cout
  Subtractor subtractor_1 (.a(Entrada_Rx), .b(Entrada_Ry), .out(subtractor_1_out));  // open: bin, bout
  assign OutOP = SUB ? subtractor_1_out : 8'bz;  // Controlled_Buffer controlled_buffer_2
  assign OutOP = MUL ? multiplier_1_out : 8'bz;  // Controlled_Buffer controlled_buffer_3
  Multiplier multiplier_1 (.a(Entrada_Rx), .b(Entrada_Ry), .out(multiplier_1_out));  // open: cin, cout
  assign controlled_buffer_4_out = EQ ? comparator_1_eq : 1'bz;  // Controlled_Buffer controlled_buffer_4
  assign controlled_buffer_4_out = LT ? comparator_2_lt : 1'bz;  // Controlled_Buffer controlled_buffer_5
  assign controlled_buffer_4_out = GT ? comparator_5_gt : 1'bz;  // Controlled_Buffer controlled_buffer_6
  assign controlled_buffer_4_out = LEQ ? or_1_out : 1'bz;  // Controlled_Buffer controlled_buffer_7
  assign controlled_buffer_4_out = GEQ ? or_2_out : 1'bz;  // Controlled_Buffer controlled_buffer_8
  assign OutCOMP = {{7{1'b0}}, controlled_buffer_4_out};  // Bit_Extender bit_extender_1
  or or_3 (or_3_out, EQ, LT, GT, LEQ, GEQ);
  assign ACULUMADOR = or_3_out ? OutCOMP : 8'bz;  // Controlled_Buffer controlled_buffer_9
  or or_4 (or_4_out, ADD, SUB, MUL);
  assign ACULUMADOR = or_4_out ? OutOP : 8'bz;  // Controlled_Buffer controlled_buffer_10

  // Other names for the same wires on the sheet: SaidaRx[7:0] = Entrada_Rx; SaidaRy[7:0] = Entrada_Ry
endmodule

module PC (
  input  CLK,
  input  reset,
  output [4:0] CONTADOR
);

  Counter #(.width(5), .max('h1f)) counter_1 (.Q(CONTADOR), .clk(CLK), .clr(reset));  // open: load, D, count, carry
endmodule

module \Registrador_de_instrução  (
  input  [7:0] Instrucao_ROM,
  input  CLK,
  input  clear,
  output [1:0] Ry,
  output [1:0] Rx,
  output [3:0] \Instrução_decodificador 
);

  Register #(.trigger("falling")) register_1 (
    .D(Instrucao_ROM), .Q({\Instrução_decodificador , Rx, Ry}), .clk(CLK), .clr(clear));  // open: en

  // Notes on the sheet:
  //   Ex:
  //   ADD RX, RY
  //   Bits mais significativos são da INSTRUÇÃO; do meio Rx, ultimos dois bits Ry
  //   01
  //   1001
  //   end Ram
  //   10
  //   end registrador
endmodule

module Banco_de_registradores (
  input  [1:0] RX,
  input  [7:0] Conteudo_RX,
  input  [1:0] Rx_2,
  input  [7:0] Input_banco,
  input  [7:0] Conteudo_Ry,
  input  [1:0] Ry,
  input  CLK,
  input  reset
);

  wire R0, R1, R2, R3;
  wire [7:0] Out_R0, Out_R1, Out_R2, Out_R3;

  Decoder #(.select(2)) decoder_1 (.out0(R0), .out1(R1), .out2(R2), .out3(R3), .sel(RX));  // open: en
  Register u_R0 (.D(Input_banco), .en(R0), .Q(Out_R0), .clk(CLK), .clr(reset));
  Register u_R1 (.D(Input_banco), .en(R1), .Q(Out_R1), .clk(CLK), .clr(reset));
  Register u_R2 (.D(Input_banco), .en(R2), .Q(Out_R2), .clk(CLK), .clr(reset));
  Register u_R3 (.D(Input_banco), .en(R3), .Q(Out_R3), .clk(CLK), .clr(reset));
  Multiplexer #(.select(2), .width(8)) multiplexer_1 (
    .in0(Out_R0), .in1(Out_R1), .in2(Out_R2), .in3(Out_R3), .out(Conteudo_RX), .sel(Rx_2));  // open: en
  Multiplexer #(.select(2), .width(8)) multiplexer_2 (
    .in0(Out_R0), .in1(Out_R1), .in2(Out_R2), .in3(Out_R3), .out(Conteudo_Ry), .sel(Ry));  // open: en

  // Other names for the same wires on the sheet: clear = reset

  // Notes on the sheet:
  //   End RAM
endmodule

module \Decode_instruções  (
  input  [3:0] Operacao,
  output EQ,
  output LT,
  output GT,
  output LEQ,
  output GEQ,
  output JMP,
  output MUL,
  output ADD,
  output SUB,
  output MovRxRy,
  output MovRxRA,
  output RDM,
  output STR,
  output HLT
);

  Comparator #(.width(4)) comparator_1 (.a(Operacao), .b(4'b0010), .eq(EQ));  // open: gt, lt
  Comparator #(.width(4)) comparator_2 (.a(Operacao), .b(4'b0011), .eq(LT));  // open: gt, lt
  Comparator #(.width(4)) comparator_3 (.a(Operacao), .b(4'b0100), .eq(GT));  // open: gt, lt
  Comparator #(.width(4)) comparator_4 (.a(Operacao), .b(4'b0101), .eq(LEQ));  // open: gt, lt
  Comparator #(.width(4)) comparator_5 (.a(Operacao), .b(4'b0110), .eq(GEQ));  // open: gt, lt
  Comparator #(.width(4)) comparator_6 (.a(Operacao), .b(4'b0111), .eq(JMP));  // open: gt, lt
  Comparator #(.width(4)) comparator_7 (.a(Operacao), .b(4'b1000), .eq(MUL));  // open: gt, lt
  Comparator #(.width(4)) comparator_8 (.a(Operacao), .b(4'b1001), .eq(ADD));  // open: gt, lt
  Comparator #(.width(4)) comparator_9 (.a(Operacao), .b(4'b1010), .eq(SUB));  // open: gt, lt
  Comparator #(.width(4)) comparator_10 (.a(Operacao), .b(4'b1011), .eq(MovRxRy));  // open: gt, lt
  Comparator #(.width(4)) comparator_11 (.a(Operacao), .b(4'b1100), .eq(MovRxRA));  // open: gt, lt
  Comparator #(.width(4)) comparator_12 (.a(Operacao), .b(4'b1101), .eq(RDM));  // open: gt, lt
  Comparator #(.width(4)) comparator_13 (.a(Operacao), .b(4'b1110), .eq(STR));  // open: gt, lt
  Comparator #(.width(4)) comparator_14 (.a(Operacao), .b(4'b1111), .eq(HLT));  // open: gt, lt
endmodule
